// Logisim project risc_processor.circ as structural Verilog: 4 circuits, main circuit main
module main (
);

  wire Clock;
  wire [31:0] pc_1_current_addr, undriven;

  Clock clock_1 (.out(Clock));
  PC pc_1 (.Clock(Clock), .Current_Addr(pc_1_current_addr));  // open: Next_Addr
  // NoConnect on undriven
  Cache Instruction_Cache (
    .En_Write(1'b0), .Address(pc_1_current_addr[15:0]), .En_Read(1'b1), .Clock(Clock), .Store_Value(undriven));  // open: Load_Value
  // also tied to GND on the sheet: {pc_1_current_addr[16], pc_1_current_addr[17], pc_1_current_addr[18], pc_1_current_addr[19], pc_1_current_addr[20], pc_1_current_addr[21], pc_1_current_addr[22], pc_1_current_addr[23], pc_1_current_addr[24], pc_1_current_addr[25], pc_1_current_addr[26], pc_1_current_addr[27], pc_1_current_addr[28], pc_1_current_addr[29], pc_1_current_addr[30], pc_1_current_addr[31]}
endmodule

module Cache (
  input  En_Write,
  input  [15:0] Address,
  input  En_Read,
  input  Clock,
  input  [31:0] Store_Value,
  output [31:0] Load_Value
);

  RAM #(.addrWidth(16), .dataWidth(32)) ram_1 (
    .addr(Address), .we(En_Write), .oe(En_Read), .clk(Clock), .din(Store_Value), .dout(Load_Value));
endmodule

module PC (
  input  [31:0] Next_Addr,
  input  Clock,
  output [31:0] Current_Addr
);

  D_Flip_Flop d_ff_1 (.D(Next_Addr[16]), .clk(Clock), .Q(Current_Addr[0]));  // open: Qn, preset, reset
  D_Flip_Flop d_ff_2 (.D(Next_Addr[17]), .clk(Clock), .Q(Current_Addr[1]));  // open: Qn, preset, reset
  D_Flip_Flop d_ff_3 (.D(Next_Addr[18]), .clk(Clock), .Q(Current_Addr[2]));  // open: Qn, preset, reset
  D_Flip_Flop d_ff_4 (.D(Next_Addr[19]), .clk(Clock), .Q(Current_Addr[3]));  // open: Qn, preset, reset
  D_Flip_Flop d_ff_5 (.D(Next_Addr[20]), .clk(Clock), .Q(Current_Addr[4]));  // open: Qn, preset, reset
  D_Flip_Flop d_ff_6 (.D(Next_Addr[21]), .clk(Clock), .Q(Current_Addr[5]));  // open: Qn, preset, reset
  D_Flip_Flop d_ff_7 (.D(Next_Addr[22]), .clk(Clock), .Q(Current_Addr[6]));  // open: Qn, preset, reset
  D_Flip_Flop d_ff_8 (.D(Next_Addr[23]), .clk(Clock), .Q(Current_Addr[7]));  // open: Qn, preset, reset
  D_Flip_Flop d_ff_9 (.D(Next_Addr[24]), .clk(Clock), .Q(Current_Addr[8]));  // open: Qn, preset, reset
  D_Flip_Flop d_ff_10 (.D(Next_Addr[25]), .clk(Clock), .Q(Current_Addr[9]));  // open: Qn, preset, reset
  D_Flip_Flop d_ff_11 (.D(Next_Addr[26]), .clk(Clock), .Q(Current_Addr[10]));  // open: Qn, preset, reset
  D_Flip_Flop d_ff_12 (.D(Next_Addr[27]), .clk(Clock), .Q(Current_Addr[11]));  // open: Qn, preset, reset
  D_Flip_Flop d_ff_13 (.D(Next_Addr[28]), .clk(Clock), .Q(Current_Addr[12]));  // open: Qn, preset, reset
  D_Flip_Flop d_ff_14 (.D(Next_Addr[29]), .clk(Clock), .Q(Current_Addr[13]));  // open: Qn, preset, reset
  D_Flip_Flop d_ff_15 (.D(Next_Addr[30]), .clk(Clock), .Q(Current_Addr[14]));  // open: Qn, preset, reset
  D_Flip_Flop d_ff_16 (.D(Next_Addr[31]), .clk(Clock), .Q(Current_Addr[15]));  // open: Qn, preset, reset
  D_Flip_Flop d_ff_17 (.D(Next_Addr[0]), .clk(Clock), .Q(Current_Addr[16]));  // open: Qn, preset, reset
  D_Flip_Flop d_ff_18 (.D(Next_Addr[1]), .clk(Clock), .Q(Current_Addr[17]));  // open: Qn, preset, reset
  D_Flip_Flop d_ff_19 (.D(Next_Addr[2]), .clk(Clock), .Q(Current_Addr[18]));  // open: Qn, preset, reset
  D_Flip_Flop d_ff_20 (.D(Next_Addr[3]), .clk(Clock), .Q(Current_Addr[19]));  // open: Qn, preset, reset
  D_Flip_Flop d_ff_21 (.D(Next_Addr[4]), .clk(Clock), .Q(Current_Addr[20]));  // open: Qn, preset, reset
  D_Flip_Flop d_ff_22 (.D(Next_Addr[5]), .clk(Clock), .Q(Current_Addr[21]));  // open: Qn, preset, reset
  D_Flip_Flop d_ff_23 (.D(Next_Addr[6]), .clk(Clock), .Q(Current_Addr[22]));  // open: Qn, preset, reset
  D_Flip_Flop d_ff_24 (.D(Next_Addr[7]), .clk(Clock), .Q(Current_Addr[23]));  // open: Qn, preset, reset
  D_Flip_Flop d_ff_25 (.D(Next_Addr[8]), .clk(Clock), .Q(Current_Addr[24]));  // open: Qn, preset, reset
  D_Flip_Flop d_ff_26 (.D(Next_Addr[9]), .clk(Clock), .Q(Current_Addr[25]));  // open: Qn, preset, reset
  D_Flip_Flop d_ff_27 (.D(Next_Addr[10]), .clk(Clock), .Q(Current_Addr[26]));  // open: Qn, preset, reset
  D_Flip_Flop d_ff_28 (.D(Next_Addr[11]), .clk(Clock), .Q(Current_Addr[27]));  // open: Qn, preset, reset
  D_Flip_Flop d_ff_29 (.D(Next_Addr[12]), .clk(Clock), .Q(Current_Addr[28]));  // open: Qn, preset, reset
  D_Flip_Flop d_ff_30 (.D(Next_Addr[13]), .clk(Clock), .Q(Current_Addr[29]));  // open: Qn, preset, reset
  D_Flip_Flop d_ff_31 (.D(Next_Addr[14]), .clk(Clock), .Q(Current_Addr[30]));  // open: Qn, preset, reset
  D_Flip_Flop d_ff_32 (.D(Next_Addr[15]), .clk(Clock), .Q(Current_Addr[31]));  // open: Qn, preset, reset

  // Other names for the same wires on the sheet: Bit_0 = Current_Addr[0]; Bit_1 = Current_Addr[1];
  //   Bit_2 = Current_Addr[2]; Bit_3 = Current_Addr[3]; Bit_4 = Current_Addr[4]; Bit_5 = Current_Addr[5];
  //   Bit_6 = Current_Addr[6]; Bit_7 = Current_Addr[7]; Bit_8 = Current_Addr[8]; Bit_9 = Current_Addr[9];
  //   Bit_10 = Current_Addr[10]; Bit_11 = Current_Addr[11]; Bit_12 = Current_Addr[12]; Bit_13 = Current_Addr[13];
  //   Bit_14 = Current_Addr[14]; Bit_15 = Current_Addr[15]; Bit_16 = Current_Addr[16]; Bit_17 = Current_Addr[17];
  //   Bit_18 = Current_Addr[18]; Bit_19 = Current_Addr[19]; Bit_20 = Current_Addr[20]; Bit_21 = Current_Addr[21];
  //   Bit_22 = Current_Addr[22]; Bit_23 = Current_Addr[23]; Bit_24 = Current_Addr[24]; Bit_25 = Current_Addr[25];
  //   Bit_26 = Current_Addr[26]; Bit_27 = Current_Addr[27]; Bit_28 = Current_Addr[28]; Bit_29 = Current_Addr[29];
  //   Bit_30 = Current_Addr[30]; Bit_31 = Current_Addr[31]
endmodule

module Decode (
  input  [31:0] Instruction,
  input  [9:0] func,
  output [4:0] rd,
  output [4:0] rs1,
  output [4:0] rs2
);

  // AND_Gate and_1 is placed but not wired

  assign Instruction[13:11] = func[2:0];
  assign rd = Instruction[10:6];
  assign rs1 = Instruction[18:14];
  assign rs2 = Instruction[23:19];

  // Other names for the same wires on the sheet: Bit_21 = Instruction[20];
  //   FI_Immediate[31:0] = {{21{Instruction[31]}}, Instruction[29:19]};
  //   FJ_Immediate[31:1] = {{12{Instruction[31]}}, Instruction[18:14], func[2:0], Instruction[19], Instruction[29:20]};
  //   Bit_22 = Instruction[21]; Bit_23 = Instruction[22]; Bit_24 = Instruction[23]; Bit_20 = Instruction[19];
  //   Bit_12 = func[0]; FU_Immediate[19:0] = {Instruction[18:14], func[2:0], {12{Instruction[31]}}}; Bit_13 = func[1];
  //   Bit_14 = func[2]; Bit_15 = Instruction[14]; Bit_16 = Instruction[15]; Bit_17 = Instruction[16];
  //   Bit_18 = Instruction[17]; Bit_19 = Instruction[18]; Bit_7 = Instruction[6];
  //   FB_Immediate[31:1] = {{20{Instruction[31]}}, Instruction[6], Instruction[29:24], Instruction[10:7]};
  //   FS_Immediate[31:0] = {{21{Instruction[31]}}, Instruction[29:24], Instruction[10:6]}; Bit_8 = Instruction[7];
  //   Bit_9 = Instruction[8]; Bit_10 = Instruction[9]; Bit_11 = Instruction[10]; Bit_25 = Instruction[24];
  //   Bit_26 = Instruction[25]; Bit_27 = Instruction[26]; Bit_28 = Instruction[27]; Bit_29 = Instruction[28];
  //   Bit_30 = Instruction[29]; Bit_31 = Instruction[31]; Opcode[5:0] = Instruction[5:0]
endmodule
